# Fritzing sketch 2D plotter (saved by Fritzing 1.0.4)
breadboards: 1

parts:
  DRV_1 = DRV 8825 Stepper Motor Carrier, High Current [part_number="DRV 8825"]
  DRV_2 = DRV 8825 Stepper Motor Carrier, High Current [part_number="DRV 8825"]
  J1-12V = Power Jack [package=power_jack_slot]
  F1 = FUSE [package=fuse_5mm]
  C2 = Electrolytic Capacitor [capacitance=100µF voltage=35V package="200 mil [THT, electrolytic]"]
  C3 = Electrolytic Capacitor [capacitance=100µF voltage=35V package="200 mil [THT, electrolytic]"]
  LED1_power = LED - 3mm [color="Red (633nm)" current=0.030A package="3 mm [THT]"]
  R1 = Resistor [tolerance=±5% resistance=220 package="2010 [SMD]"]
  7805 = Voltage Regulator - 5V [package="TO220 [THT]"]
  C4 = Electrolytic Capacitor [capacitance=1000μF voltage=35V package="1010 [SMD, electrolytic]"]
  C5 = Electrolytic Capacitor [capacitance=1000μF voltage=35V package="1010 [SMD, electrolytic]"]
  C6_104 = Capacitor [package=cap-pth-small2]
  C6_105 = Capacitor [package=cap-pth-small2]
  DC1 = Hirose DF13 Series Header [part_number=DF13#-4P-1.25V package=DF13C-4P-1.25V]
  DC2 = Hirose DF13 Series Header [part_number=DF13#-4P-1.25V package=DF13C-4P-1.25V]
  R2ctht_10k = Resistor [tolerance=±5% resistance=220 package="2512 [SMD]"]
  Linh_kiện1 = Arduino Nano (Rev3.0)
  J3 = Camdenboss CTB0158-2 [part_number=CTB0158-2 package=THT]
  R2ctht_10k1 = Resistor [tolerance=±5% resistance=220 package="2512 [SMD]"]
  J4 = Camdenboss CTB0158-2 [part_number=CTB0158-2 package=THT]
  SW1 = DIP Switch 8 Position [package=dipswitch-08]
  servo = Hirose DF13 Series Header [part_number=DF13A-3P-1.25H package=DF13A-3P-1.25H]

nets:
  N1: DRV_1.MS1, SW1.3
  N2: DRV_1.MS2, SW1.2
  N3: DRV_1.MS3, SW1.1
  N4: DRV_1.RESET, DRV_1.SLEEP
  N5: DRV_1.STEP, Linh_kiện1.D10
  N6: DRV_1.DIRECTION, Linh_kiện1.D9
  N7: DRV_1.VOLTAGE_ST/_MT, F1.2, C2.+, 7805.input_voltage, C4.+, C6_104.1, Linh_kiện1.VIN
  GND: DRV_1.GROUND_ST/_MT, DRV_1.GROUND_LOG, DRV_2.GROUND_ST/_MT, DRV_2.GROUND_LOG, J1-12V.GNDBREAK, J1-12V.GND, C2.-, C3.-, LED1_power.cathode, 7805.GND, C4.-, C5.-, C6_104.2, C6_105.2, Linh_kiện1.GND, servo.1
  N8: DRV_1.OUT_2B, DC1.1
  N9: DRV_1.OUT_2A, DC1.2
  N10: DRV_1.OUT_1A, DC1.3
  N11: DRV_1.OUT_1B, DC1.4
  N12: DRV_1.VOLTAGE_DD, DRV_2.VOLTAGE_DD, R1.Pin_0, 7805.output_voltage, C5.+, C6_105.1, R2ctht_10k.Pin_0, R2ctht_10k1.Pin_1, servo.3
  N13: DRV_2.MS1, SW1.6
  N14: DRV_2.MS2, SW1.5
  N15: DRV_2.MS3, SW1.4
  N16: DRV_2.RESET, DRV_2.SLEEP
  N17: DRV_2.STEP, Linh_kiện1.D8
  N18: DRV_2.DIRECTION, Linh_kiện1.D7
  N19: DRV_2.VOLTAGE_ST/_MT, C3.+
  N20: DRV_2.OUT_2B, DC2.1
  N21: DRV_2.OUT_2A, DC2.2
  N22: DRV_2.OUT_1A, DC2.3
  N23: DRV_2.OUT_1B, DC2.4
  N24: J1-12V.PWR, F1.1
  N25: LED1_power.anode, R1.Pin_1, SW1.11, SW1.12, SW1.13, SW1.14, SW1.15, SW1.16
  N26: R2ctht_10k.Pin_1, Linh_kiện1.D6, J3.pin1
  N27: Linh_kiện1.D5, R2ctht_10k1.Pin_0, J4.pin1
  N28: Linh_kiện1.D11/MOSI, servo.2
  N29: J3.pin2, J4.pin2
